# Fritzing sketch microgrid_connection_unit_v0_1 (saved by Fritzing 0.9.6b)
breadboards: 1

parts:
  Q1 = Basic FET P-Channel [package="TO220 [THT]"]
  Q2 = Basic FET P-Channel [package="TO220 [THT]"]
  R1 = Resistor [tolerance=±5% power=0.25 resistance=10k package=THT]
  Q3 = NPN-Transistor [package="TO92 [THT]"]
  R2 = Resistor [tolerance=±5% power=0.25 resistance=1k package=THT]
  Part1 = Arduino Nano 33 IOT
  R3 = Resistor [tolerance=±5% power=0.25 resistance=100k package=THT]
  R4 = Resistor [tolerance=±5% power=0.25 resistance=100k package=THT]
  R5 = Resistor [tolerance=±5% power=0.25 resistance=10k package=THT]
  R6 = Resistor [tolerance=±5% power=0.25 resistance=10k package=THT]
  J2 = Screw terminal - 2 pins [package=THT]
  Part2 = ACS712 Current Sensor Module
  J1 = Screw terminal - 2 pins [package=THT]

nets:
  N1: Q1.gate, Q2.gate, R1.Pin_0, Q3.C
  N2: Q1.drain, Part1.VIN, R3.Pin_1, J2.pin2
  N3: Q1.source, Q2.source, R1.Pin_1
  N4: Q2.drain, R4.Pin_0, Part2.INPUT+
  GND: Q3.E, Part1.GND, R5.Pin_0, R6.Pin_0, J2.pin1, Part2.GND, J1.pin2
  N5: Q3.B, R2.Pin_1
  D2: R2.Pin_0, Part1.D2
  A2: Part1.A2, Part2.OUT
  A1: Part1.A1, R4.Pin_1, R5.Pin_1
  A0: Part1.A0, R3.Pin_0, R6.Pin_1
  5V: Part1.+5V, Part2.VCC
  N6: Part2.INPUT-, J1.pin1

notes:
  local system
  grid

custom parts:
  Arduino Nano 33 IOT: The Arduino Nano 33 IoT is the easiest and cheapest point of entry to enhance existing devices (and creating new ones) to be part of the IoT and designing pico-network applications. Whether you are looking at building a sensor network connected to your office or home router, or if you want to create a BLE device sending data to a cellphone, the Nano 33 IoT is your one-stop-solution for many of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
